# Fritzing sketch LED_Resistor_Calculator (2) (saved by Fritzing 0.9.3b)
breadboards: 1

parts:
  Part1 = Arduino Uno (Rev3) - ICSP
  LCD1 = LCD screen
  LED1 = smd LED [color="Red (633nm)" package="1206 [SMD]"]
  LED2 = smd LED [color="Orange (612nm)" package="1206 [SMD]"]
  LED3 = smd LED [color="Green (570nm)" package="1206 [SMD]"]
  LED4 = smd LED [color="Blue (430nm)" package="1206 [SMD]"]
  LED5 = smd LED [color="White (4500K)" package="1206 [SMD]"]
  S1 = Momentary Switch [package=ksa_sealed_tac_switch]
  S2 = Momentary Switch [package=ksa_sealed_tac_switch]
  S3 = Momentary Switch [package=ksa_sealed_tac_switch]
  S4 = Momentary Switch [package=ksa_sealed_tac_switch]
  S5 = Momentary Switch [package=ksa_sealed_tac_switch]
  R1 = Resistor [tolerance=±5% resistance=220 package="2512 [SMD]"]
  R2 = Resistor [tolerance=±5% resistance=100 package="2512 [SMD]"]
  R3 = Resistor [tolerance=±5% resistance=330 package="2512 [SMD]"]
  R4 = Resistor [tolerance=±5% resistance=680 package="2512 [SMD]"]
  part = Resistor [tolerance=±5% resistance=10k package="2512 [SMD]"]
  part_2 = Resistor [tolerance=±5% resistance=10k package="2512 [SMD]"]
  part_3 = Resistor [tolerance=±5% resistance=10k package="2512 [SMD]"]
  part_4 = Resistor [tolerance=±5% resistance=10k package="2512 [SMD]"]
  part_5 = Resistor [tolerance=±5% resistance=10k package="2512 [SMD]"]
  unknown_R5 = Resistor [tolerance=±5% resistance=470 package="2512 [SMD]"]

nets:
  N1: Part1.A1, LCD1.R/W
  N2: Part1.A2, LCD1.E
  GND: Part1.GND, LCD1.VSS, LED1.cathode, LED2.cathode, LED3.cathode, LED4.cathode, LED5.cathode, part.Pin_0, part_2.Pin_0, part_3.Pin_0, part_4.Pin_0, part_5.Pin_0
  N3: Part1.D2, S2.1
  N4: Part1.D3_PWM, S1.1
  N5: Part1.D4, S3.1
  N6: Part1.D5_PWM, S4.1
  N7: Part1.D6_PWM, S5.1
  5V: Part1.5V, LCD1.VDD, R1.Pin_0, R2.Pin_0, R3.Pin_0, R4.Pin_0, unknown_R5.Pin_0
  N8: LED1.anode, S2.4, R1.Pin_1
  N9: LED2.anode, S1.4, R2.Pin_1
  N10: LED3.anode, S3.4, R3.Pin_1
  N11: LED4.anode, S4.4, R4.Pin_1
  N12: LED5.anode, S5.4, unknown_R5.Pin_1
  N13: S1.2, part_2.Pin_1
  N14: S2.2, part.Pin_1
  N15: S3.2, part_3.Pin_1
  N16: S4.2, part_5.Pin_1
  N17: S5.2, part_4.Pin_1
